// Logisim project sap-1.circ as structural Verilog: 3 circuits, main circuit main
module main (
);

  wire AI, AO, BI, CE, CLK, clock_1_out, CO, EO, FI, HL, II, IO, J, MI, not_1_out, OI, RI, RO, RS, SU;
  wire [1:0] adder_1_cout, FLAG;
  wire [2:0] Step_q;
  wire [3:0] IR_q, IR_q_2;
  wire [7:0] A_q, adder_1_out, B_q, controlled_buffer_2_out, controlled_buffer_3_out,
       controlled_buffer_9_out, controlled_buffer_10_out, controlled_buffer_11_out, MAR_q, OUT_q, PC_q,
       ram_1_data, xor_1_out;
  wire [11:0] bin_bcd_1_bcd;

  Clock clock_1 (.out(clock_1_out));
  assign CLK = not_1_out ? clock_1_out : 1'bz;  // Controlled_Buffer controlled_buffer_1
  not not_1 (not_1_out, HL);
  Register MAR (.D(controlled_buffer_2_out), .Q(MAR_q), .clk(CLK), .clr(RS));  // open: en
  Register IR (.D(controlled_buffer_3_out), .Q({IR_q, IR_q_2}), .clk(CLK), .clr(RS));  // open: en
  Counter #(.width(3), .max('h4), .trigger("falling")) Step (
    .Q(Step_q), .clk(CLK), .clr(RS));  // open: load, D, count, carry
  assign controlled_buffer_2_out = MI ? ram_1_data : 8'bz;  // Controlled_Buffer controlled_buffer_2
  RAM #(.bus("separate")) ram_1 (
    .addr(MAR_q), .din(ram_1_data), .data(ram_1_data), .str(RI), .clk(CLK), .ld(RO));  // open: sel, clr
  assign controlled_buffer_3_out = II ? ram_1_data : 8'bz;  // Controlled_Buffer controlled_buffer_3
  assign ram_1_data = IO ? {4'b0000, IR_q_2} : 8'bz;  // Controlled_Buffer controlled_buffer_4
  ROM #(.addrWidth(9), .dataWidth(16)) rom_1 (
    .addr({FLAG, IR_q, Step_q}), .data({HL, CO, MI, CE, RI, RO, II, IO, AI, AO, BI, EO, OI, SU, J, FI}));  // open: sel
  // Probe on ram_1_data
  assign ram_1_data = CO ? PC_q : 8'bz;  // Controlled_Buffer controlled_buffer_5
  assign ram_1_data = AO ? A_q : 8'bz;  // Controlled_Buffer controlled_buffer_6
  assign ram_1_data = 1'b0 ? B_q : 8'bz;  // Controlled_Buffer controlled_buffer_7
  assign ram_1_data = EO ? adder_1_out : 8'bz;  // Controlled_Buffer controlled_buffer_8
  Button Reset (.out(RS));
  Counter PC (.load(J), .D(ram_1_data), .count(CE), .Q(PC_q), .clk(CLK), .clr(RS));  // open: carry
  Register A (.D(controlled_buffer_9_out), .Q(A_q), .clk(CLK), .clr(RS));  // open: en
  assign controlled_buffer_9_out = AI ? ram_1_data : 8'bz;  // Controlled_Buffer controlled_buffer_9
  Register B (.D(controlled_buffer_10_out), .Q(B_q), .clk(CLK), .clr(RS));  // open: en
  assign controlled_buffer_10_out = BI ? ram_1_data : 8'bz;  // Controlled_Buffer controlled_buffer_10
  assign controlled_buffer_11_out = OI ? ram_1_data : 8'bz;  // Controlled_Buffer controlled_buffer_11
  Register OUT (.D(controlled_buffer_11_out), .Q(OUT_q), .clk(CLK), .clr(RS));  // open: en
  assign xor_1_out = {8{SU}} ^ B_q;  // XOR_Gate xor_1, 8 bits wide
  bin_bcd bin_bcd_1 (.BIN(OUT_q), .BCD(bin_bcd_1_bcd));
  Hex_Digit_Display hex_digit_display_1 (.value(bin_bcd_1_bcd[11:8]));  // open: dp
  // Probe on adder_1_out
  Adder adder_1 (.a(A_q), .b(xor_1_out), .out(adder_1_out), .cin(SU), .cout(adder_1_cout[0]));
  Hex_Digit_Display hex_digit_display_2 (.value(bin_bcd_1_bcd[7:4]));  // open: dp
  Hex_Digit_Display hex_digit_display_3 (.value(bin_bcd_1_bcd[3:0]));  // open: dp
  Comparator comparator_1 (.a(adder_1_out), .b({8{1'b0}}), .eq(adder_1_cout[1]));  // open: gt, lt
  // Probe on FLAG
  Register #(.width(2)) u_Flag (.D(adder_1_cout), .en(FI), .Q(FLAG), .clk(CLK), .clr(RS));

  // Notes on the sheet:
  //   RAM
  //   CU
  //   Control Word
  //   contents of rom_1 (hex, n*v repeats v):
  //   6000 1600 8000 5*0 6000 1600 2100 480 4*0 6000 1600 2100 420 91 0 0 0 6000 1600 2100 420 95 0 0 0
  //   6000 1600 2100 840 4*0 6000 1600 180 5*0 6000 1600 102 5*0 6000 1600 48 5*0 6000 1600 6*0 6000 1600
  //   54*0 6000 1600 8000 5*0 6000 1600 2100 480 4*0 6000 1600 2100 420 91 0 0 0 6000 1600 2100 420 95 0 0
  //   0 6000 1600 2100 840 4*0 6000 1600 180 5*0 6000 1600 102 5*0 6000 1600 48 5*0 6000 1600 6*0 6000
  //   1600 102 53*0 6000 1600 8000 5*0 6000 1600 2100 480 4*0 6000 1600 2100 420 91 0 0 0 6000 1600 2100
  //   420 95 0 0 0 6000 1600 2100 840 4*0 6000 1600 180 5*0 6000 1600 102 5*0 6000 1600 48 5*0 6000 1600
  //   102 5*0 6000 1600 54*0 6000 1600 8000 5*0 6000 1600 2100 480 4*0 6000 1600 2100 420 91 0 0 0 6000
  //   1600 2100 420 95 0 0 0 6000 1600 2100 840 4*0 6000 1600 180 5*0 6000 1600 102 5*0 6000 1600 48 5*0
  //   6000 1600 102 5*0 6000 1600 102 50*0 6175 7269 7a61
endmodule

module bin_bcd (
  input  [7:0] BIN,
  output [11:0] BCD
);

  wire add3_1_s0, add3_1_s1, add3_1_s2, add3_1_s3, add3_2_s0, add3_2_s1, add3_2_s2, add3_2_s3, add3_3_s0,
       add3_3_s1, add3_3_s2, add3_3_s3, add3_4_s0, add3_4_s1, add3_4_s2, add3_4_s3, add3_5_s0, add3_5_s1,
       add3_5_s2;

  add3 add3_1 (
    .B3(1'b0), .B2(BIN[7]), .B1(BIN[6]), .B0(BIN[5]), .S3(add3_1_s3), .S2(add3_1_s2), .S1(add3_1_s1),
    .S0(add3_1_s0));
  add3 add3_2 (
    .B3(add3_3_s2), .B2(add3_3_s1), .B1(add3_3_s0), .B0(BIN[3]), .S3(add3_2_s3), .S2(add3_2_s2),
    .S1(add3_2_s1), .S0(add3_2_s0));
  add3 add3_3 (
    .B3(add3_1_s2), .B2(add3_1_s1), .B1(add3_1_s0), .B0(BIN[4]), .S3(add3_3_s3), .S2(add3_3_s2),
    .S1(add3_3_s1), .S0(add3_3_s0));
  add3 add3_4 (
    .B3(add3_2_s2), .B2(add3_2_s1), .B1(add3_2_s0), .B0(BIN[2]), .S3(add3_4_s3), .S2(add3_4_s2),
    .S1(add3_4_s1), .S0(add3_4_s0));
  add3 add3_5 (
    .B3(1'b0), .B2(add3_1_s3), .B1(add3_3_s3), .B0(add3_2_s3), .S3(BCD[9]), .S2(add3_5_s2), .S1(add3_5_s1),
    .S0(add3_5_s0));
  add3 add3_6 (
    .B3(add3_4_s2), .B2(add3_4_s1), .B1(add3_4_s0), .B0(BIN[1]), .S3(BCD[4]), .S2(BCD[3]), .S1(BCD[2]),
    .S0(BCD[1]));
  add3 add3_7 (
    .B3(add3_5_s2), .B2(add3_5_s1), .B1(add3_5_s0), .B0(add3_4_s3), .S3(BCD[8]), .S2(BCD[7]), .S1(BCD[6]),
    .S0(BCD[5]));

  assign {BCD[11:10], BCD[0]} = {2'b00, BIN[0]};
endmodule

module add3 (
  input  B3,
  input  B2,
  input  B1,
  input  B0,
  output S3,
  output S2,
  output S1,
  output S0
);

  wire and_1_out, and_2_out, and_3_out, and_4_out, and_5_out, and_6_out, and_7_out, and_8_out, and_9_out,
       and_10_out, not_1_out, not_2_out, not_3_out, not_4_out, not_5_out, not_6_out, not_7_out, not_8_out;

  and and_1 (and_1_out, B2, B0);
  and and_2 (and_2_out, B2, B1);
  and and_3 (and_3_out, B2, not_1_out, not_2_out);
  not not_1 (not_1_out, B1);
  not not_2 (not_2_out, B0);
  and and_4 (and_4_out, B3, B0);
  not not_3 (not_3_out, B2);
  and and_5 (and_5_out, not_3_out, B1);
  and and_6 (and_6_out, B1, B0);
  and and_7 (and_7_out, B3, not_4_out);
  not not_4 (not_4_out, B0);
  not not_5 (not_5_out, B3);
  not not_6 (not_6_out, B2);
  and and_8 (and_8_out, not_5_out, not_6_out, B0);
  and and_9 (and_9_out, B2, B1, not_7_out);
  not not_7 (not_7_out, B0);
  and and_10 (and_10_out, B3, not_8_out);
  not not_8 (not_8_out, B0);
  or or_1 (S3, and_1_out, and_2_out, B3);
  or or_2 (S2, and_3_out, and_4_out);
  or or_3 (S1, and_5_out, and_6_out, and_7_out);
  or or_4 (S0, and_8_out, and_9_out, and_10_out);
endmodule
